# Fritzing sketch sketch (saved by Fritzing 0.9.3b)
breadboards: 1

parts:
  Part1 = Arduino Nano (Rev3.0) (ICSP)
  U1 = LM386 [package=dip08]
  VCC1 = Battery block 9V
  R1 = Resistor [tolerance=±5% resistance=10 package="2010 [SMD]"]
  C1 = Tantalum Capacitor [capacitance=0.1µF package="A 3216 [SMD, tantalum]"]
  SP1 = SPEAKER [package=pcb_mount_speaker]
  R2 = Trimmer Potentiometer [maximum_resistance=10kΩ package=THT]
  C3 = Electrolytic Capacitor [capacitance=10µF package="1010 [SMD, electrolytic]"]
  R3 = Trimmer Potentiometer [maximum_resistance=10kΩ package=THT]
  C4 = Tantalum Capacitor [capacitance=0.1mF package="A 3216 [SMD, tantalum]"]
  C2 = Electrolytic Capacitor [capacitance=1000μF package="1010 [SMD, electrolytic]"]

nets:
  N1: Part1.GND, U1.-IN, U1.V-, VCC1.-, R1.Pin_0, SP1.+
  N2: Part1.D3, U1.+IN
  N3: Part1.VIN, U1.V+, VCC1.+
  N4: U1.GAIN, R2.wiper, C3.-, R3.leg1
  N5: U1.OUT, C1.+, C4.+, C2.+
  N6: SP1.-, C2.-
  N7: R2.leg1, C3.+
  N8: R3.wiper, C4.-
